// Digital circuit 8bit_alu.dig as structural Verilog
module _8bit_alu (
  input  [7:0] N,
  input  [2:0] OP,
  input  CLK,
  input  En,
  output [7:0] AC,
  output [7:0] MQ,
  output [15:0] plenis
);

  wire and_1_out, and_2_out, not_1_out, not_2_out, not_3_out;
  wire [1:0] and_4_out;
  wire [7:0] Div_Quo, Div_Rem, Mult_LSB, Mult_MSB, multiplexer_1_out, multiplexer_2_out, NAND, Sum_Sub, XOR;

  LED led_1 (.in(MQ[7]));
  LED led_2 (.in(MQ[5]));
  LED led_3 (.in(MQ[6]));
  LED led_4 (.in(MQ[3]));
  LED led_5 (.in(MQ[4]));
  LED led_6 (.in(MQ[1]));
  LED led_7 (.in(MQ[2]));
  LED led_8 (.in(MQ[0]));
  // _8bit_adder_subtractor _8bit_adder_subtractor_1: pin names not known; wires that end beside it: OP[0], AC, N, Sum_Sub
  // _8bit_multiplier _8bit_multiplier_1: pin names not known; wires that end beside it: AC, N, {Mult_MSB, Mult_LSB}
  // _8bit_divider _8bit_divider_1: pin names not known; wires that end beside it: AC, N, Div_Rem, Div_Quo
  assign NAND = ~(AC & N);  // NAnd nand_1, 8 bits wide
  assign XOR = AC ^ N;  // XOr xor_1, 8 bits wide
  LED led_9 (.in(AC[7]));
  LED led_10 (.in(AC[5]));
  LED led_11 (.in(AC[6]));
  LED led_12 (.in(AC[3]));
  LED led_13 (.in(AC[4]));
  LED led_14 (.in(AC[1]));
  LED led_15 (.in(AC[2]));
  LED led_16 (.in(AC[0]));
  Multiplexer #(.Bits(8), .Selector_Bits(3)) multiplexer_1 (
    .sel(OP), .in_0(Sum_Sub), .in_1(Sum_Sub), .in_2(Mult_LSB), .in_3(Div_Rem), .in_4({AC[6:0], 1'b0}),
    .in_5({1'b0, AC[7:1]}), .in_6(NAND), .in_7(XOR), .out(multiplexer_1_out));
  Seven_Seg_Hex seven_seg_hex_1 (.d(MQ[7:4]), .dp(1'b0));
  Seven_Seg_Hex seven_seg_hex_2 (.d(MQ[3:0]), .dp(1'b0));
  not not_1 (not_1_out, OP[0]);
  Register #(.Bits(8)) u_AC (.D(multiplexer_1_out), .C(CLK), .en(En), .Q(AC));
  and and_1 (and_1_out, not_1_out, OP[1]);
  and and_2 (and_2_out, OP[0], OP[1]);
  Seven_Seg_Hex seven_seg_hex_3 (.d(AC[7:4]), .dp(1'b0));
  and and_3 (and_4_out[0], and_1_out, not_2_out);
  not not_2 (not_2_out, OP[2]);
  and and_4 (and_4_out[1], and_2_out, not_3_out);
  not not_3 (not_3_out, OP[2]);
  Seven_Seg_Hex seven_seg_hex_4 (.d(AC[3:0]), .dp(1'b0));
  Multiplexer #(.Bits(8), .Selector_Bits(3)) multiplexer_2 (
    .sel({1'b0, and_4_out}), .in_0({8{1'b0}}), .in_1(Mult_MSB), .in_2(Div_Quo), .in_3({8{1'b0}}),
    .in_4({8{1'b0}}), .in_5({8{1'b0}}), .in_6({8{1'b0}}), .in_7({8{1'b0}}), .out(multiplexer_2_out));
  Register #(.Bits(8)) u_MQ (.D(multiplexer_2_out), .C(CLK), .en(En), .Q(MQ));

  assign plenis = {MQ, AC};

  // Other names for the same wires on the sheet: Shift_L[7:1] = AC[6:0]; Shift_R[6:0] = AC[7:1]

  // Notes on the sheet:
  //   Operation select (OP)
  //   0: AC+N
  //   1: AC-N
  //   2: AC*B
  //   3: AC/N
  //   4: AC shift left
  //   5: AC shift right
  //   6: AC NAND N
  //   7: AC XOR N
endmodule
